// Logisim project DecoderNew.circ as structural Verilog: 6 circuits, main circuit DecodeNew
module DecodeNew (
  input  [63:0] WRITE_MEMORY,
  input  [63:0] WRITE_EXECUTION,
  input  [3:0] icode,
  input  [3:0] rA,
  input  [3:0] rB,
  input  CLK,
  input  FETCH_DONE,
  output [3:0] ICODE2,
  output [1:0] READ_WRITE_STATUS,
  output [63:0] VAL_A,
  output [63:0] VAL_B,
  output [63:0] rax,
  output [63:0] rcx,
  output [63:0] rdx,
  output [63:0] rbx,
  output [63:0] rsp,
  output [63:0] rbp,
  output [63:0] rsi,
  output [63:0] rdi,
  output [63:0] r8,
  output [63:0] r9,
  output [63:0] r10,
  output [63:0] r11,
  output [63:0] r12,
  output [63:0] r13,
  output [63:0] r14
);

  wire and_1_out, and_2_out, comparator_1_lt, nor_1_out, not_1_out;
  wire [3:0] dste_1_result, dstm_1_result, srca_1_result, srcb_1_result;
  wire [7:0] counter_1_q;

  srcA srca_1 (.rA(rA), .icode(icode), .result(srca_1_result));
  srcB srcb_1 (.rB(rB), .icode(icode), .result(srcb_1_result));
  dstE dste_1 (.rB(rB), .icode(icode), .result(dste_1_result));
  dstM dstm_1 (.rA(rA), .icode(icode), .result(dstm_1_result));
  RegisterFile registerfile_1 (
    .W_Memory(WRITE_MEMORY), .W_Execution(WRITE_EXECUTION), .source_A(srca_1_result),
    .dst_Memory(dstm_1_result), .Timer(CLK), .source_B(srcb_1_result), .dst_Execution(dste_1_result),
    .fetch_Done(FETCH_DONE), .Timing_output(READ_WRITE_STATUS), .value_A(VAL_A), .value_B(VAL_B), .rax(rax),
    .rcx(rcx), .rdx(rdx), .rbx(rbx), .rsp(rsp), .rbp(rbp), .rsi(rsi), .rdi(rdi), .r8(r8), .r9(r9), .r10(r10),
    .r11(r11), .r12(r12), .r13(r13), .r14(r14));
  nor nor_1 (nor_1_out, READ_WRITE_STATUS[0], READ_WRITE_STATUS[1]);
  and and_1 (and_1_out, nor_1_out, FETCH_DONE);
  not not_1 (not_1_out, FETCH_DONE);
  Counter counter_1 (.clr(not_1_out), .up(1'b1), .clk(CLK), .Q(counter_1_q));  // open: load, count, D, carry
  Comparator comparator_1 (.a(counter_1_q), .b(8'h4), .lt(comparator_1_lt));  // open: gt, eq
  and and_2 (and_2_out, and_1_out, comparator_1_lt);
  Multiplexer #(.width(4)) multiplexer_1 (.in0(4'b0000), .in1(icode), .out(ICODE2), .sel(and_2_out));
endmodule

module srcA (
  input  [3:0] rA,
  input  [3:0] icode,
  output [3:0] result
);

  wire decoder_1_out0, decoder_1_out1, decoder_1_out2, decoder_1_out3, decoder_1_out4, decoder_1_out5,
       decoder_1_out6, decoder_1_out7, decoder_1_out8, decoder_1_out9, decoder_1_out10, decoder_1_out11,
       decoder_1_out12, decoder_1_out13, decoder_1_out14, decoder_1_out15, or_1_out, or_2_out, or_3_out;

  Decoder #(.select(4)) decoder_1 (
    .out0(decoder_1_out0), .out1(decoder_1_out1), .out2(decoder_1_out2), .out3(decoder_1_out3),
    .out4(decoder_1_out4), .out5(decoder_1_out5), .out6(decoder_1_out6), .out7(decoder_1_out7),
    .out8(decoder_1_out8), .out9(decoder_1_out9), .out10(decoder_1_out10), .out11(decoder_1_out11),
    .out12(decoder_1_out12), .out13(decoder_1_out13), .out14(decoder_1_out14), .out15(decoder_1_out15),
    .sel(icode));  // open: en
  or or_1 (or_1_out, decoder_1_out11, decoder_1_out12);
  assign result = or_1_out ? 4'b0100 : 4'bz;  // Controlled_Buffer controlled_buffer_1
  assign result = or_2_out ? 4'b1111 : 4'bz;  // Controlled_Buffer controlled_buffer_2
  or or_2 (or_2_out, decoder_1_out0, decoder_1_out1, decoder_1_out3, decoder_1_out5, decoder_1_out7);
  or or_3 (or_3_out, decoder_1_out2, decoder_1_out4, decoder_1_out6);
  assign result = or_3_out ? rA : 4'bz;  // Controlled_Buffer controlled_buffer_3
endmodule

module srcB (
  input  [3:0] rB,
  input  [3:0] icode,
  output [3:0] result
);

  wire decoder_1_out0, decoder_1_out1, decoder_1_out2, decoder_1_out3, decoder_1_out4, decoder_1_out5,
       decoder_1_out6, decoder_1_out7, decoder_1_out8, decoder_1_out9, decoder_1_out10, decoder_1_out11,
       decoder_1_out12, decoder_1_out13, decoder_1_out14, decoder_1_out15, or_1_out, or_2_out, or_3_out;

  Decoder #(.select(4)) decoder_1 (
    .out0(decoder_1_out0), .out1(decoder_1_out1), .out2(decoder_1_out2), .out3(decoder_1_out3),
    .out4(decoder_1_out4), .out5(decoder_1_out5), .out6(decoder_1_out6), .out7(decoder_1_out7),
    .out8(decoder_1_out8), .out9(decoder_1_out9), .out10(decoder_1_out10), .out11(decoder_1_out11),
    .out12(decoder_1_out12), .out13(decoder_1_out13), .out14(decoder_1_out14), .out15(decoder_1_out15),
    .sel(icode));  // open: en
  or or_1 (or_1_out, decoder_1_out11, decoder_1_out12);
  assign result = or_2_out ? 4'b1111 : 4'bz;  // Controlled_Buffer controlled_buffer_1
  or or_2 (or_2_out, decoder_1_out0, decoder_1_out1, decoder_1_out2, decoder_1_out3, decoder_1_out7);
  assign result = or_1_out ? 4'b0100 : 4'bz;  // Controlled_Buffer controlled_buffer_2
  or or_3 (or_3_out, decoder_1_out4, decoder_1_out5, decoder_1_out6);
  assign result = or_3_out ? rB : 4'bz;  // Controlled_Buffer controlled_buffer_3
endmodule

module dstM (
  input  [3:0] rA,
  input  [3:0] icode,
  output [3:0] result
);

  wire decoder_1_out0, decoder_1_out1, decoder_1_out2, decoder_1_out3, decoder_1_out4, decoder_1_out5,
       decoder_1_out6, decoder_1_out7, decoder_1_out8, decoder_1_out9, decoder_1_out10, decoder_1_out11,
       decoder_1_out12, decoder_1_out13, decoder_1_out14, decoder_1_out15, or_1_out, or_2_out;

  Decoder #(.select(4)) decoder_1 (
    .out0(decoder_1_out0), .out1(decoder_1_out1), .out2(decoder_1_out2), .out3(decoder_1_out3),
    .out4(decoder_1_out4), .out5(decoder_1_out5), .out6(decoder_1_out6), .out7(decoder_1_out7),
    .out8(decoder_1_out8), .out9(decoder_1_out9), .out10(decoder_1_out10), .out11(decoder_1_out11),
    .out12(decoder_1_out12), .out13(decoder_1_out13), .out14(decoder_1_out14), .out15(decoder_1_out15),
    .sel(icode));  // open: en
  or or_1 (or_1_out, decoder_1_out0, decoder_1_out1, decoder_1_out2, decoder_1_out3, decoder_1_out4, decoder_1_out6, decoder_1_out7, decoder_1_out11);
  assign result = or_1_out ? 4'b1111 : 4'bz;  // Controlled_Buffer controlled_buffer_1
  assign result = or_2_out ? rA : 4'bz;  // Controlled_Buffer controlled_buffer_2
  or or_2 (or_2_out, decoder_1_out5, decoder_1_out12);
endmodule

module dstE (
  input  [3:0] rB,
  input  [3:0] icode,
  output [3:0] result
);

  wire decoder_1_out0, decoder_1_out1, decoder_1_out2, decoder_1_out3, decoder_1_out4, decoder_1_out5,
       decoder_1_out6, decoder_1_out7, decoder_1_out8, decoder_1_out9, decoder_1_out10, decoder_1_out11,
       decoder_1_out12, decoder_1_out13, decoder_1_out14, decoder_1_out15, or_1_out, or_2_out, or_3_out;

  Decoder #(.select(4)) decoder_1 (
    .out0(decoder_1_out0), .out1(decoder_1_out1), .out2(decoder_1_out2), .out3(decoder_1_out3),
    .out4(decoder_1_out4), .out5(decoder_1_out5), .out6(decoder_1_out6), .out7(decoder_1_out7),
    .out8(decoder_1_out8), .out9(decoder_1_out9), .out10(decoder_1_out10), .out11(decoder_1_out11),
    .out12(decoder_1_out12), .out13(decoder_1_out13), .out14(decoder_1_out14), .out15(decoder_1_out15),
    .sel(icode));  // open: en
  or or_1 (or_1_out, decoder_1_out11, decoder_1_out12);
  or or_2 (or_2_out, decoder_1_out0, decoder_1_out1, decoder_1_out4, decoder_1_out5, decoder_1_out7);
  assign result = or_1_out ? 4'b0100 : 4'bz;  // Controlled_Buffer controlled_buffer_1
  assign result = or_2_out ? 4'b1111 : 4'bz;  // Controlled_Buffer controlled_buffer_2
  assign result = or_3_out ? rB : 4'bz;  // Controlled_Buffer controlled_buffer_3
  or or_3 (or_3_out, decoder_1_out2, decoder_1_out3, decoder_1_out6);
endmodule

module RegisterFile (
  input  [63:0] W_Memory,
  input  [63:0] W_Execution,
  input  [3:0] source_A,
  input  [3:0] dst_Memory,
  input  Timer,
  input  [3:0] source_B,
  input  [3:0] dst_Execution,
  input  fetch_Done,
  output [1:0] Timing_output,
  output [63:0] value_A,
  output [63:0] value_B,
  output [63:0] rax,
  output [63:0] rcx,
  output [63:0] rdx,
  output [63:0] rbx,
  output [63:0] rsp,
  output [63:0] rbp,
  output [63:0] rsi,
  output [63:0] rdi,
  output [63:0] r8,
  output [63:0] r9,
  output [63:0] r10,
  output [63:0] r11,
  output [63:0] r12,
  output [63:0] r13,
  output [63:0] r14
);

  wire and_1_out, and_2_out, and_4_out, and_5_out, and_8_out, decoder_1_out0, decoder_1_out1, decoder_1_out2,
       decoder_1_out3, decoder_1_out4, decoder_1_out5, decoder_1_out6, decoder_1_out7, decoder_1_out8,
       decoder_1_out9, decoder_1_out10, decoder_1_out11, decoder_1_out12, decoder_1_out13, decoder_1_out14,
       decoder_1_out15, decoder_2_out0, decoder_2_out1, decoder_2_out2, decoder_2_out3, decoder_2_out4,
       decoder_2_out5, decoder_2_out6, decoder_2_out7, decoder_2_out8, decoder_2_out9, decoder_2_out10,
       decoder_2_out12, decoder_2_out13, decoder_2_out14, decoder_2_out15, decoder_3_out0, decoder_3_out1,
       decoder_3_out2, decoder_3_out3, decoder_3_out4, decoder_3_out5, decoder_3_out6, decoder_3_out7,
       decoder_3_out8, decoder_3_out9, decoder_3_out10, decoder_3_out11, decoder_3_out12, decoder_3_out13,
       decoder_3_out14, decoder_4_out0, decoder_4_out1, decoder_4_out2, decoder_4_out3, decoder_4_out4,
       decoder_4_out5, decoder_4_out6, decoder_4_out7, decoder_4_out8, decoder_4_out9, decoder_4_out10,
       decoder_4_out11, decoder_4_out12, decoder_4_out13, decoder_4_out14, decoder_4_out15, nor_1_out,
       not_1_out, not_2_out, or_1_out, or_2_out, or_3_out, or_4_out, or_5_out, or_6_out, or_7_out, or_8_out,
       or_9_out, or_10_out, or_11_out, or_12_out, or_13_out, or_14_out, or_15_out, S0_q, S1_q;
  wire [63:0] controlled_buffer_1_out, controlled_buffer_2_out, controlled_buffer_3_out,
       controlled_buffer_5_out, controlled_buffer_7_out, controlled_buffer_9_out, controlled_buffer_11_out,
       controlled_buffer_13_out, controlled_buffer_15_out, controlled_buffer_17_out,
       controlled_buffer_19_out, controlled_buffer_22_out, controlled_buffer_26_out,
       controlled_buffer_30_out, controlled_buffer_34_out, controlled_buffer_41_out,
       controlled_buffer_45_out, RF_DNE_q, undriven;

  and and_1 (and_1_out, fetch_Done, Timing_output[0]);
  and and_2 (and_2_out, fetch_Done, Timing_output[1]);
  Decoder #(.select(4)) decoder_1 (
    .out0(decoder_1_out0), .out1(decoder_1_out1), .out2(decoder_1_out2), .out3(decoder_1_out3),
    .out4(decoder_1_out4), .out5(decoder_1_out5), .out6(decoder_1_out6), .out7(decoder_1_out7),
    .out8(decoder_1_out8), .out9(decoder_1_out9), .out10(decoder_1_out10), .out11(decoder_1_out11),
    .out12(decoder_1_out12), .out13(decoder_1_out13), .out14(decoder_1_out14), .out15(decoder_1_out15),
    .sel(dst_Memory), .en(and_2_out));
  // AND_Gate and_3 is placed but not wired
  assign controlled_buffer_1_out = Timing_output[1] ? W_Memory : 64'bz;  // Controlled_Buffer controlled_buffer_1
  assign controlled_buffer_2_out = Timing_output[0] ? W_Execution : 64'bz;  // Controlled_Buffer controlled_buffer_2
  Decoder #(.select(4)) decoder_2 (
    .out0(decoder_2_out0), .out1(decoder_2_out1), .out2(decoder_2_out2), .out3(decoder_2_out3),
    .out4(decoder_2_out4), .out5(decoder_2_out5), .out6(decoder_2_out6), .out7(decoder_2_out7),
    .out8(decoder_2_out8), .out9(decoder_2_out9), .out10(decoder_2_out10), .out11(decoder_1_out11),
    .out12(decoder_2_out12), .out13(decoder_2_out13), .out14(decoder_2_out14), .out15(decoder_2_out15),
    .sel(dst_Execution), .en(and_1_out));
  assign controlled_buffer_3_out = decoder_2_out0 ? controlled_buffer_2_out : 64'bz;  // Controlled_Buffer controlled_buffer_3
  Register #(.width(64)) R0_rax (.D(controlled_buffer_3_out), .en(or_1_out), .clk(Timer), .Q(rax));  // open: clr
  assign controlled_buffer_3_out = decoder_1_out0 ? controlled_buffer_1_out : 64'bz;  // Controlled_Buffer controlled_buffer_4
  or or_1 (or_1_out, decoder_2_out0, decoder_1_out0);
  assign controlled_buffer_5_out = decoder_2_out2 ? controlled_buffer_2_out : 64'bz;  // Controlled_Buffer controlled_buffer_5
  Register #(.width(64)) R2_rdx (.D(controlled_buffer_5_out), .en(or_2_out), .clk(Timer), .Q(rdx));  // open: clr
  assign controlled_buffer_5_out = decoder_1_out2 ? controlled_buffer_1_out : 64'bz;  // Controlled_Buffer controlled_buffer_6
  or or_2 (or_2_out, decoder_1_out2, decoder_2_out2);
  assign controlled_buffer_7_out = decoder_2_out4 ? controlled_buffer_2_out : 64'bz;  // Controlled_Buffer controlled_buffer_7
  Register #(.width(64)) R4_rsp (.D(controlled_buffer_7_out), .en(or_3_out), .clk(Timer), .Q(rsp));  // open: clr
  assign controlled_buffer_7_out = decoder_1_out4 ? controlled_buffer_1_out : 64'bz;  // Controlled_Buffer controlled_buffer_8
  or or_3 (or_3_out, decoder_1_out4, decoder_2_out4);
  assign controlled_buffer_9_out = decoder_2_out6 ? controlled_buffer_2_out : 64'bz;  // Controlled_Buffer controlled_buffer_9
  Register #(.width(64)) R6_rsi (.D(controlled_buffer_9_out), .en(or_4_out), .clk(Timer), .Q(rsi));  // open: clr
  assign controlled_buffer_9_out = decoder_1_out6 ? controlled_buffer_1_out : 64'bz;  // Controlled_Buffer controlled_buffer_10
  or or_4 (or_4_out, decoder_2_out6, decoder_1_out6);
  assign controlled_buffer_11_out = decoder_2_out8 ? controlled_buffer_2_out : 64'bz;  // Controlled_Buffer controlled_buffer_11
  Register #(.width(64)) R8_r8 (.D(controlled_buffer_11_out), .en(or_5_out), .clk(Timer), .Q(r8));  // open: clr
  assign controlled_buffer_11_out = decoder_1_out8 ? controlled_buffer_1_out : 64'bz;  // Controlled_Buffer controlled_buffer_12
  or or_5 (or_5_out, decoder_2_out8, decoder_1_out8);
  assign controlled_buffer_13_out = decoder_2_out10 ? controlled_buffer_2_out : 64'bz;  // Controlled_Buffer controlled_buffer_13
  Register #(.width(64)) R10_r10 (.D(controlled_buffer_13_out), .en(or_6_out), .clk(Timer), .Q(r10));  // open: clr
  assign controlled_buffer_13_out = decoder_1_out10 ? controlled_buffer_1_out : 64'bz;  // Controlled_Buffer controlled_buffer_14
  or or_6 (or_6_out, decoder_2_out10, decoder_1_out10);
  assign controlled_buffer_15_out = decoder_2_out12 ? controlled_buffer_2_out : 64'bz;  // Controlled_Buffer controlled_buffer_15
  Register #(.width(64)) R12_r12 (.D(controlled_buffer_15_out), .en(or_7_out), .clk(Timer), .Q(r12));  // open: clr
  assign controlled_buffer_15_out = decoder_1_out12 ? controlled_buffer_1_out : 64'bz;  // Controlled_Buffer controlled_buffer_16
  or or_7 (or_7_out, decoder_2_out12, decoder_1_out12);
  assign controlled_buffer_17_out = decoder_2_out14 ? controlled_buffer_2_out : 64'bz;  // Controlled_Buffer controlled_buffer_17
  Register #(.width(64)) R14_r14 (.D(controlled_buffer_17_out), .en(or_8_out), .clk(Timer), .Q(r14));  // open: clr
  assign controlled_buffer_17_out = decoder_1_out14 ? controlled_buffer_1_out : 64'bz;  // Controlled_Buffer controlled_buffer_18
  or or_8 (or_8_out, decoder_2_out14, decoder_1_out14);
  D_Flip_Flop S1 (.D(and_4_out), .clk(Timer), .Q(S1_q));  // open: Qn, preset, reset
  D_Flip_Flop S0 (.D(and_5_out), .clk(Timer), .Q(S0_q));  // open: Qn, preset, reset
  assign controlled_buffer_19_out = decoder_2_out9 ? controlled_buffer_2_out : 64'bz;  // Controlled_Buffer controlled_buffer_19
  assign value_A = decoder_4_out0 ? rax : 64'bz;  // Controlled_Buffer controlled_buffer_20
  assign value_B = decoder_3_out0 ? rax : 64'bz;  // Controlled_Buffer controlled_buffer_21
  assign controlled_buffer_22_out = decoder_1_out1 ? undriven : 64'bz;  // Controlled_Buffer controlled_buffer_22
  or or_9 (or_9_out, decoder_1_out1, decoder_2_out1);
  assign controlled_buffer_22_out = decoder_2_out1 ? controlled_buffer_2_out : 64'bz;  // Controlled_Buffer controlled_buffer_23
  assign value_A = decoder_4_out2 ? rdx : 64'bz;  // Controlled_Buffer controlled_buffer_24
  assign value_B = decoder_3_out2 ? rdx : 64'bz;  // Controlled_Buffer controlled_buffer_25
  assign controlled_buffer_26_out = decoder_2_out3 ? controlled_buffer_2_out : 64'bz;  // Controlled_Buffer controlled_buffer_26
  assign controlled_buffer_26_out = decoder_1_out3 ? controlled_buffer_1_out : 64'bz;  // Controlled_Buffer controlled_buffer_27
  assign value_A = decoder_4_out4 ? rsp : 64'bz;  // Controlled_Buffer controlled_buffer_28
  assign value_B = decoder_3_out4 ? rsp : 64'bz;  // Controlled_Buffer controlled_buffer_29
  assign controlled_buffer_30_out = decoder_2_out5 ? controlled_buffer_2_out : 64'bz;  // Controlled_Buffer controlled_buffer_30
  assign controlled_buffer_30_out = decoder_1_out5 ? controlled_buffer_1_out : 64'bz;  // Controlled_Buffer controlled_buffer_31
  assign value_A = decoder_4_out6 ? rsi : 64'bz;  // Controlled_Buffer controlled_buffer_32
  assign value_B = decoder_3_out6 ? rsi : 64'bz;  // Controlled_Buffer controlled_buffer_33
  assign controlled_buffer_34_out = decoder_2_out7 ? controlled_buffer_2_out : 64'bz;  // Controlled_Buffer controlled_buffer_34
  assign controlled_buffer_34_out = decoder_1_out7 ? controlled_buffer_1_out : 64'bz;  // Controlled_Buffer controlled_buffer_35
  assign value_A = decoder_4_out8 ? r8 : 64'bz;  // Controlled_Buffer controlled_buffer_36
  assign value_B = decoder_3_out8 ? r8 : 64'bz;  // Controlled_Buffer controlled_buffer_37
  assign controlled_buffer_19_out = decoder_1_out9 ? controlled_buffer_1_out : 64'bz;  // Controlled_Buffer controlled_buffer_38
  or or_10 (or_10_out, decoder_1_out9, decoder_2_out9);
  assign value_A = decoder_4_out10 ? r10 : 64'bz;  // Controlled_Buffer controlled_buffer_39
  assign value_B = decoder_3_out10 ? r10 : 64'bz;  // Controlled_Buffer controlled_buffer_40
  assign controlled_buffer_41_out = decoder_1_out11 ? controlled_buffer_2_out : 64'bz;  // Controlled_Buffer controlled_buffer_41
  assign controlled_buffer_41_out = decoder_1_out11 ? controlled_buffer_1_out : 64'bz;  // Controlled_Buffer controlled_buffer_42
  assign value_A = decoder_4_out12 ? r12 : 64'bz;  // Controlled_Buffer controlled_buffer_43
  assign value_B = decoder_3_out12 ? r12 : 64'bz;  // Controlled_Buffer controlled_buffer_44
  assign controlled_buffer_45_out = decoder_2_out13 ? controlled_buffer_2_out : 64'bz;  // Controlled_Buffer controlled_buffer_45
  assign controlled_buffer_45_out = decoder_1_out13 ? controlled_buffer_1_out : 64'bz;  // Controlled_Buffer controlled_buffer_46
  assign value_A = decoder_4_out14 ? r14 : 64'bz;  // Controlled_Buffer controlled_buffer_47
  assign value_B = decoder_3_out14 ? r14 : 64'bz;  // Controlled_Buffer controlled_buffer_48
  not not_1 (not_1_out, S1_q);
  not not_2 (not_2_out, S0_q);
  Register #(.width(64)) R1_rcx (.D(controlled_buffer_22_out), .en(or_9_out), .clk(Timer), .Q(rcx));  // open: clr
  Register #(.width(64)) R3_rbx (.D(controlled_buffer_26_out), .en(or_11_out), .clk(Timer), .Q(rbx));  // open: clr
  or or_11 (or_11_out, decoder_2_out3, decoder_1_out3);
  Register #(.width(64)) R5_rbp (.D(controlled_buffer_30_out), .en(or_12_out), .clk(Timer), .Q(rbp));  // open: clr
  or or_12 (or_12_out, decoder_2_out5, decoder_1_out5);
  Register #(.width(64)) R7_rdi (.D(controlled_buffer_34_out), .en(or_13_out), .clk(Timer), .Q(rdi));  // open: clr
  or or_13 (or_13_out, decoder_2_out7, decoder_1_out7);
  Register #(.width(64)) R9_r9 (.D(controlled_buffer_19_out), .en(or_10_out), .clk(Timer), .Q(r9));  // open: clr
  Register #(.width(64)) R11_r11 (.D(controlled_buffer_41_out), .en(or_14_out), .clk(Timer), .Q(r11));  // open: clr
  or or_14 (or_14_out, decoder_1_out11, decoder_1_out11);
  Register #(.width(64)) R13_r13 (.D(controlled_buffer_45_out), .en(or_15_out), .clk(Timer), .Q(r13));  // open: clr
  or or_15 (or_15_out, decoder_1_out13, decoder_2_out13);
  Register #(.width(64)) RF_DNE (.en(decoder_1_out15), .clk(Timer), .Q(RF_DNE_q));  // open: D, clr
  and and_4 (and_4_out, not_1_out, S0_q);
  and and_5 (and_5_out, not_1_out, not_2_out);
  and and_6 (Timing_output[1], S1_q, not_2_out);
  and and_7 (Timing_output[0], not_1_out, S0_q);
  assign value_A = decoder_4_out1 ? rcx : 64'bz;  // Controlled_Buffer controlled_buffer_49
  assign value_B = decoder_3_out1 ? rcx : 64'bz;  // Controlled_Buffer controlled_buffer_50
  assign value_A = decoder_4_out3 ? rbx : 64'bz;  // Controlled_Buffer controlled_buffer_51
  assign value_B = decoder_3_out3 ? rbx : 64'bz;  // Controlled_Buffer controlled_buffer_52
  assign value_A = decoder_4_out5 ? rbp : 64'bz;  // Controlled_Buffer controlled_buffer_53
  assign value_B = decoder_3_out5 ? rbp : 64'bz;  // Controlled_Buffer controlled_buffer_54
  assign value_A = decoder_4_out7 ? rdi : 64'bz;  // Controlled_Buffer controlled_buffer_55
  assign value_B = decoder_3_out7 ? rdi : 64'bz;  // Controlled_Buffer controlled_buffer_56
  assign value_A = decoder_4_out9 ? r9 : 64'bz;  // Controlled_Buffer controlled_buffer_57
  assign value_B = decoder_3_out9 ? r9 : 64'bz;  // Controlled_Buffer controlled_buffer_58
  assign value_A = decoder_4_out11 ? r11 : 64'bz;  // Controlled_Buffer controlled_buffer_59
  assign value_B = decoder_3_out11 ? r11 : 64'bz;  // Controlled_Buffer controlled_buffer_60
  assign value_A = decoder_4_out13 ? r13 : 64'bz;  // Controlled_Buffer controlled_buffer_61
  assign value_B = decoder_3_out13 ? r13 : 64'bz;  // Controlled_Buffer controlled_buffer_62
  Controlled_Buffer #(.width(64)) controlled_buffer_63 (.in(RF_DNE_q), .en(decoder_4_out15));  // open: out
  Controlled_Buffer #(.width(64)) controlled_buffer_64 ();  // open: in, out, en
  nor nor_1 (nor_1_out, Timing_output[1], Timing_output[0]);
  Decoder #(.select(4)) decoder_3 (
    .out0(decoder_3_out0), .out1(decoder_3_out1), .out2(decoder_3_out2), .out3(decoder_3_out3),
    .out4(decoder_3_out4), .out5(decoder_3_out5), .out6(decoder_3_out6), .out7(decoder_3_out7),
    .out8(decoder_3_out8), .out9(decoder_3_out9), .out10(decoder_3_out10), .out11(decoder_3_out11),
    .out12(decoder_3_out12), .out13(decoder_3_out13), .out14(decoder_3_out14), .sel(source_B), .en(and_8_out));  // open: out15
  Decoder #(.select(4)) decoder_4 (
    .out0(decoder_4_out0), .out1(decoder_4_out1), .out2(decoder_4_out2), .out3(decoder_4_out3),
    .out4(decoder_4_out4), .out5(decoder_4_out5), .out6(decoder_4_out6), .out7(decoder_4_out7),
    .out8(decoder_4_out8), .out9(decoder_4_out9), .out10(decoder_4_out10), .out11(decoder_4_out11),
    .out12(decoder_4_out12), .out13(decoder_4_out13), .out14(decoder_4_out14), .out15(decoder_4_out15),
    .sel(source_A), .en(and_8_out));
  and and_8 (and_8_out, nor_1_out, fetch_Done);

  // Notes on the sheet:
  //   Now done with
  //   Dire wire
  //   reading and writing the same
  //   register
  //   Ok so we could be retarded
  //   Also is the question of enable or not
  //   look into enable
  //   ALSO ALSO the problem of
  //   2 things, one is how do we write both memory and eval
  //   and mirror what we did on the other side
  //   THE REGISTER FILE
endmodule
